# Fritzing sketch Day-02 (saved by Fritzing 0.9.10b)
breadboards: 1

parts:
  LED1 = LED - 5mm [color="Red (633nm)" current=0.030 package="5 mm [THT]"]
  R1 = Resistor [tolerance=±5% power=0.25 resistance=220 package=THT]
  Part1 = Inventr HERO

nets:
  N1: LED1.cathode, Part1.GND
  N2: LED1.anode, R1.Pin_1
  N3: R1.Pin_0, Part1.D12/MISO

notes:
  220 Ohm current limiting resistor

custom parts:
  Inventr HERO: The inventr hero is a microcontroller board based on the ATmega328 (datasheet). It has 14 digital input/output pins (of which 6 can be used as PWM outputs), 6 analog inputs, a 16 MHz ceramic resonator, a USB connection, a power jack, an ICSP header, and a reset button. It contains everything needed to support the microcontroller; simply connect it to a computer with a USB cable or power it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
