# Fritzing sketch Day-04 (saved by Fritzing 0.9.10b)
breadboards: 1

parts:
  Part1 = Inventr HERO
  LED5 = LED - 5mm [color="Green (565nm)" current=30mA package="5 mm [THT]"]
  LED6 = LED - 5mm [color="Blue (470nm)" current=30mA package="5 mm [THT]"]
  LED7 = LED - 5mm [color="Red (633nm)" current=0.030 package="5 mm [THT]"]
  R13 = Resistor [tolerance=±5% power=0.25 resistance=220 package=THT]
  R14 = Resistor [tolerance=±5% power=0.25 resistance=10k package=THT]
  R15 = Resistor [tolerance=±5% power=0.25 resistance=10k package=THT]
  R16 = Resistor [tolerance=±5% power=0.25 resistance=10k package=THT]
  R17 = Resistor [tolerance=±5% power=0.25 resistance=220 package=THT]
  R18 = Resistor [tolerance=±5% power=0.25 resistance=220 package=THT]
  S1 = DIP Switch 3 Position

nets:
  N1: Part1.D10_PWM/SS, R13.Pin_0
  N2: Part1.D11_PWM/MOSI, R17.Pin_0
  N3: Part1.D12/MISO, R18.Pin_0
  N4: Part1.GND, LED5.cathode, LED6.cathode, LED7.cathode, R14.Pin_0, R15.Pin_0, R16.Pin_0
  N5: Part1.D2, R14.Pin_1
  N6: Part1.D3_PWM, R15.Pin_1
  N7: Part1.D4, R16.Pin_1
  N8: Part1.5V, S1.1, S1.2, S1.3
  N9: LED5.anode, R18.Pin_1
  N10: LED6.anode, R17.Pin_1
  N11: LED7.anode, R13.Pin_1

notes:
  10K Ohm resistors for pull-down
  220 Ohm resistors used to provide proper current for LEDs

custom parts:
  Inventr HERO: The inventr hero is a microcontroller board based on the ATmega328 (datasheet). It has 14 digital input/output pins (of which 6 can be used as PWM outputs), 6 analog inputs, a 16 MHz ceramic resonator, a USB connection, a power jack, an ICSP header, and a reset button. It contains everything needed to support the microcontroller; simply connect it to a computer with a USB cable or power it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
