# Fritzing sketch Day4 (saved by Fritzing 0.9.10b)
breadboards: 1

parts:
  Part2 = Arduino Uno (Inventr.io)
  LED4 = LED - 5mm [color="Green (565nm)" current=30mA package="5 mm [THT]"]
  LED5 = LED - 5mm [color="Blue (470nm)" current=30mA package="5 mm [THT]"]
  LED6 = LED - 5mm [color="Red (633nm)" current=0.030 package="5 mm [THT]"]
  R7 = Resistor [tolerance=±5% power=0.25 resistance=220 package=THT]
  R8 = Resistor [tolerance=±5% power=0.25 resistance=220 package=THT]
  R9 = Resistor [tolerance=±5% power=0.25 resistance=220 package=THT]
  R10 = Resistor [tolerance=±5% power=0.25 resistance=220 package=THT]
  R11 = Resistor [tolerance=±5% power=0.25 resistance=220 package=THT]
  R12 = Resistor [tolerance=±5% power=0.25 resistance=220 package=THT]
  S2 = DIP Switch 3 Position

nets:
  N1: Part2.D10_PWM/SS, R11.Pin_0
  N2: Part2.D11_PWM/MOSI, R10.Pin_0
  N3: Part2.D12/MISO, R12.Pin_0
  N4: Part2.GND, LED4.cathode, LED5.cathode, LED6.cathode, R7.Pin_0, R8.Pin_0, R9.Pin_0
  N5: Part2.D2, R7.Pin_1
  N6: Part2.D3_PWM, R8.Pin_1
  N7: Part2.D4, R9.Pin_1
  N8: Part2.5V, S2.1, S2.2, S2.3
  N9: LED4.anode, R12.Pin_1
  N10: LED5.anode, R10.Pin_1
  N11: LED6.anode, R11.Pin_1

custom parts:
  Arduino Uno (Inventr.io): The Arduino Uno is a microcontroller board based on the ATmega328 (datasheet). It has 14 digital input/output pins (of which 6 can be used as PWM outputs), 6 analog inputs, a 16 MHz ceramic resonator, a USB connection, a power jack, an ICSP header, and a reset button. It contains everything needed to support the microcontroller; simply connect it to a computer with a USB cable or power it with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
