# Fritzing sketch Day-06 (saved by Fritzing 0.9.10b)
breadboards: 1

parts:
  R1 = Resistor [tolerance=±5% power=0.25 resistance=220 package=THT]
  R2 = PHOTOCELL [package=photocell]  # not connected
  Part2 = Inventr HERO

nets:
  N1: R1.Pin_0, Part2.A0
  N2: R1.Pin_1, Part2.GND

custom parts:
  Inventr HERO: The inventr hero is a microcontroller board based on the ATmega328 (datasheet). It has 14 digital input/output pins (of which 6 can be used as PWM outputs), 6 analog inputs, a 16 MHz ceramic resonator, a USB connection, a power jack, an ICSP header, and a reset button. It contains everything needed to support the microcontroller; simply connect it to a computer with a USB cable or power it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
