# Fritzing sketch Day-09 (saved by Fritzing 0.9.10b)
breadboards: 1

parts:
  LED1 = RGB LED (com. cathode, rgb) [package="5 mm [THT]"]
  R1 = Resistor [tolerance=±5% power=0.25 resistance=220 package=THT]
  R2 = Resistor [tolerance=±5% power=0.25 resistance=220 package=THT]
  R3 = Resistor [tolerance=±5% power=0.25 resistance=220 package=THT]
  R4 = Resistor [tolerance=±5% power=0.25 resistance=220 package=THT]
  R5 = PHOTOCELL [package=photocell]
  Part2 = Inventr HERO

nets:
  N1: LED1.red_anode, R1.Pin_1
  N2: LED1.common_cathode, R4.Pin_1, Part2.GND
  N3: LED1.green_anode, R2.Pin_1
  N4: LED1.blue_anode, R3.Pin_1
  N5: R1.Pin_0, Part2.D11_PWM/MOSI
  N6: R2.Pin_0, Part2.D10_PWM/SS
  N7: R3.Pin_0, Part2.D9_PWM
  N8: R4.Pin_0, R5.P$1, Part2.A0
  N9: R5.P$2, Part2.5V

custom parts:
  Inventr HERO: The inventr hero is a microcontroller board based on the ATmega328 (datasheet). It has 14 digital input/output pins (of which 6 can be used as PWM outputs), 6 analog inputs, a 16 MHz ceramic resonator, a USB connection, a power jack, an ICSP header, and a reset button. It contains everything needed to support the microcontroller; simply connect it to a computer with a USB cable or power it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
