# Fritzing sketch Day-11 (saved by Fritzing 0.9.10b)

parts:
  Generic_4x4_button_keypad1 = Generic 4x4 Keypad
  Part1 = Inventr HERO

nets:
  N1: Generic_4x4_button_keypad1.C4, Part1.D9_PWM
  N2: Generic_4x4_button_keypad1.C3, Part1.D8
  N3: Generic_4x4_button_keypad1.C2, Part1.D7
  N4: Generic_4x4_button_keypad1.C1, Part1.D6_PWM
  N5: Generic_4x4_button_keypad1.R1, Part1.D5_PWM
  N6: Generic_4x4_button_keypad1.R2, Part1.D4
  N7: Generic_4x4_button_keypad1.R3, Part1.D3_PWM
  N8: Generic_4x4_button_keypad1.R4, Part1.D2

custom parts:
  Generic 4x4 Keypad: generic 4x4 keypad 4 rows of four 6 mm tact switches cheap and nasty but works
  Inventr HERO: The inventr hero is a microcontroller board based on the ATmega328 (datasheet). It has 14 digital input/output pins (of which 6 can be used as PWM outputs), 6 analog inputs, a 16 MHz ceramic resonator, a USB connection, a power jack, an ICSP header, and a reset button. It contains everything needed to support the microcontroller; simply connect it to a computer with a USB cable or power it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
