# Fritzing sketch Day16 (saved by Fritzing 0.9.10b)

parts:
  Part1 = Arduino Uno (Inventr.io)
  inventr2 = Inventr.io 4 Digit 7 Segment Display [part_number=HW-069]

nets:
  N1: Part1.D5_PWM, inventr2.DIO
  N2: Part1.D6_PWM, inventr2.CLK
  5V: Part1.5V, inventr2.VCC
  GND: Part1.GND, inventr2.GND

custom parts:
  Arduino Uno (Inventr.io): The Arduino Uno is a microcontroller board based on the ATmega328 (datasheet). It has 14 digital input/output pins (of which 6 can be used as PWM outputs), 6 analog inputs, a 16 MHz ceramic resonator, a USB connection, a power jack, an ICSP header, and a reset button. It contains everything needed to support the microcontroller; simply connect it to a computer with a USB cable or power it with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
  Inventr.io 4 Digit 7 Segment Display: Inventr.io 4 digit 7 segment display fritzing file for the 30 Days Lost in Space Course
