# Fritzing sketch Day-18 (saved by Fritzing 0.9.10b)
breadboards: 1

parts:
  inventr2 = Inventr.io 4 Digit 7 Segment Display [part_number=HW-069]
  Part2 = Inventr HERO
  RE1 = KY-040 Rotary encoder [package=THT]

nets:
  GND: inventr2.GND, Part2.GND, RE1.GND
  VCC: inventr2.VCC, Part2.5V, RE1.Vcc
  N1: inventr2.DIO, Part2.D5_PWM
  N2: inventr2.CLK, Part2.D6_PWM
  N3: Part2.D2, RE1.CLK
  N4: Part2.D3_PWM, RE1.DT

custom parts:
  Inventr.io 4 Digit 7 Segment Display: Inventr.io 4 digit 7 segment display fritzing file for the 30 Days Lost in Space Course
  Inventr HERO: The inventr hero is a microcontroller board based on the ATmega328 (datasheet). It has 14 digital input/output pins (of which 6 can be used as PWM outputs), 6 analog inputs, a 16 MHz ceramic resonator, a USB connection, a power jack, an ICSP header, and a reset button. It contains everything needed to support the microcontroller; simply connect it to a computer with a USB cable or power it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
  KY-040 Rotary encoder: KY-040 Rotary Encoder with switch on breakout borad from AZ Delivery
