# Fritzing sketch Day-23 (saved by Fritzing 0.9.10b)
breadboards: 1

parts:
  OLED_I2C1 = OLED 128x64 I2C Monochrome Display
  Part2 = Inventr HERO
  inventr1 = Inventr.io 4 Digit 7 Segment Display [part_number=HW-069]

nets:
  N1: OLED_I2C1.SDA, Part2.A4/SDA
  N2: OLED_I2C1.SCK, Part2.A5/SCL
  VDD: OLED_I2C1.VDD, Part2.5V, inventr1.VCC
  GND: OLED_I2C1.GND, Part2.GND, inventr1.GND
  N3: Part2.D4, inventr1.DIO
  N4: Part2.D5_PWM, inventr1.CLK

notes:
  Keep this side clear for more components coming tomorrow!

custom parts:
  Inventr HERO: The inventr hero is a microcontroller board based on the ATmega328 (datasheet). It has 14 digital input/output pins (of which 6 can be used as PWM outputs), 6 analog inputs, a 16 MHz ceramic resonator, a USB connection, a power jack, an ICSP header, and a reset button. It contains everything needed to support the microcontroller; simply connect it to a computer with a USB cable or power it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
  Inventr.io 4 Digit 7 Segment Display: Inventr.io 4 digit 7 segment display fritzing file for the 30 Days Lost in Space Course
