# Fritzing sketch Day-27 (saved by Fritzing 0.9.10b)
breadboards: 1

parts:
  Part1 = Arduino Uno (Inventr.io)
  OLED_I2C1 = OLED 128x64 I2C Monochrome Display
  S1 = DIP Switch 3 Position
  R1 = Resistor [tolerance=±5% power=0.25 resistance=220 package=THT]
  R2 = Resistor [tolerance=±5% power=0.25 resistance=220 package=THT]
  R3 = Resistor [tolerance=±5% power=0.25 resistance=220 package=THT]
  LED1 = LED - 5mm [color="Red (633nm)" current=0.030 package="5 mm [THT]"]
  R4 = Resistor [tolerance=±5% power=0.25 resistance=220 package=THT]
  Generic_4x4_button_keypad1 = Generic 4x4 Keypad
  RE1 = KY-040 Rotary encoder [package=THT]

nets:
  N1: Part1.A1, RE1.CLK
  N2: Part1.A2, RE1.DT
  N3: Part1.A3, RE1.SW
  N4: Part1.A4/SDA, OLED_I2C1.SDA
  N5: Part1.A5/SCL, OLED_I2C1.SCK
  N6: Part1.D8, Generic_4x4_button_keypad1.R2
  N7: Part1.D9_PWM, Generic_4x4_button_keypad1.R1
  N8: Part1.D10_PWM/SS, Generic_4x4_button_keypad1.C1
  N9: Part1.D11_PWM/MOSI, Generic_4x4_button_keypad1.C2
  N10: Part1.D12/MISO, Generic_4x4_button_keypad1.C3
  N11: Part1.D13/SCK, Generic_4x4_button_keypad1.C4
  GND: Part1.GND, OLED_I2C1.GND, R1.Pin_1, R2.Pin_1, R3.Pin_1, R4.Pin_1, RE1.GND
  N12: Part1.D2, S1.1, R1.Pin_0
  N13: Part1.D3_PWM, S1.2, R2.Pin_0
  N14: Part1.D4, S1.3, R3.Pin_0
  N15: Part1.D5_PWM, LED1.anode
  N16: Part1.D6_PWM, Generic_4x4_button_keypad1.R4
  N17: Part1.D7, Generic_4x4_button_keypad1.R3
  N18: Part1.5V#84, S1.4, S1.5, S1.6, RE1.Vcc
  N19: Part1.5V#87, OLED_I2C1.VDD
  N20: LED1.cathode, R4.Pin_0

custom parts:
  Arduino Uno (Inventr.io): The Arduino Uno is a microcontroller board based on the ATmega328 (datasheet). It has 14 digital input/output pins (of which 6 can be used as PWM outputs), 6 analog inputs, a 16 MHz ceramic resonator, a USB connection, a power jack, an ICSP header, and a reset button. It contains everything needed to support the microcontroller; simply connect it to a computer with a USB cable or power it with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
  Generic 4x4 Keypad: generic 4x4 keypad 4 rows of four 6 mm tact switches cheap and nasty but works
  KY-040 Rotary encoder: KY-040 Rotary Encoder with switch on breakout borad from AZ Delivery
