# Fritzing sketch Day-29 (saved by Fritzing 0.9.10b)
breadboards: 1

parts:
  OLED_I2C1 = OLED 128x64 I2C Monochrome Display
  Part2 = Inventr HERO
  inventr2 = Inventr.io 4 Digit 7 Segment Display [part_number=HW-069]
  S2 = DIP Switch 3 Position
  R8 = Resistor [tolerance=±5% power=0.25 resistance=10k package=THT]
  R9 = Resistor [tolerance=±5% power=0.25 resistance=10k package=THT]
  R10 = Resistor [tolerance=±5% power=0.25 resistance=10k package=THT]
  Generic_4x4_button_keypad2 = Generic 4x4 Keypad
  RE2 = KY-040 Rotary encoder [package=THT]

nets:
  N1: OLED_I2C1.SDA, Part2.A4/SDA
  N2: OLED_I2C1.SCK, Part2.A5/SCL
  VCC: OLED_I2C1.VDD, Part2.5V, inventr2.VCC, S2.4, S2.5, S2.6, RE2.Vcc
  GND: OLED_I2C1.GND, Part2.GND, inventr2.GND, R8.Pin_1, R9.Pin_1, RE2.GND
  N3: Part2.A0, S2.1, R10.Pin_0
  N4: Part2.A1, S2.2, R9.Pin_0
  N5: Part2.A2, S2.3, R8.Pin_0
  N6: Part2.D8, Generic_4x4_button_keypad2.R2
  N7: Part2.D9_PWM, Generic_4x4_button_keypad2.R1
  N8: Part2.D10_PWM/SS, Generic_4x4_button_keypad2.C1
  N9: Part2.D11_PWM/MOSI, Generic_4x4_button_keypad2.C2
  N10: Part2.D12/MISO, Generic_4x4_button_keypad2.C3
  N11: Part2.D13/SCK, Generic_4x4_button_keypad2.C4
  N12: Part2.D2, inventr2.DIO
  N13: Part2.D3_PWM, inventr2.CLK
  N14: Part2.D4, RE2.DT
  N15: Part2.D5_PWM, RE2.CLK
  N16: Part2.D6_PWM, Generic_4x4_button_keypad2.R4
  N17: Part2.D7, Generic_4x4_button_keypad2.R3

custom parts:
  Inventr HERO: The inventr hero is a microcontroller board based on the ATmega328 (datasheet). It has 14 digital input/output pins (of which 6 can be used as PWM outputs), 6 analog inputs, a 16 MHz ceramic resonator, a USB connection, a power jack, an ICSP header, and a reset button. It contains everything needed to support the microcontroller; simply connect it to a computer with a USB cable or power it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
  Inventr.io 4 Digit 7 Segment Display: Inventr.io 4 digit 7 segment display fritzing file for the 30 Days Lost in Space Course
  Generic 4x4 Keypad: generic 4x4 keypad 4 rows of four 6 mm tact switches cheap and nasty but works
  KY-040 Rotary encoder: KY-040 Rotary Encoder with switch on breakout borad from AZ Delivery
